// Logisim project FrequencyCounter.circ as structural Verilog: 3 circuits, main circuit Dflipflop
// PLL
module PhaseLockLoop (
  input  [1:0] in_1,
  input  [1:0] in_2,
  output out_3,
  output f,
  output f_2,
  output f_4,
  output f_8,
  output out_8,
  output out_9,
  output out_10
);

  wire clk_out, clock_1_out, d_ff_1_qn, d_ff_2_qn, d_ff_3_qn, frequencycounter_1_f_4;

  Clock clk (.out(clk_out));
  not not_1 (f, clk_out);
  Clock clock_1 (.out(clock_1_out));
  D_Flip_Flop d_ff_1 (.clk(clk_out), .D(d_ff_1_qn), .Q(f_2), .Qn(d_ff_1_qn));  // open: preset, en, reset
  FrequencyCounter frequencycounter_1 (
    .Sel(in_2), .f(out_10), .f_2(out_9), .f_4(frequencycounter_1_f_4), .f_8(out_8), .out_2(clock_1_out));
  D_Flip_Flop d_ff_2 (.clk(d_ff_1_qn), .D(d_ff_2_qn), .Q(f_4), .Qn(d_ff_2_qn));  // open: preset, en, reset
  D_Flip_Flop d_ff_3 (.clk(d_ff_2_qn), .D(d_ff_3_qn), .Q(f_8), .Qn(d_ff_3_qn));  // open: preset, en, reset
  Multiplexer #(.select(2), .enable("false")) multiplexer_1 (
    .in0(f_8), .in1(f_4), .in2(f_2), .in3(f), .out(out_3), .sel(in_1));
endmodule

module Dflipflop (
  input  D,
  input  CLK,
  output Q,
  output Q_prime
);

  wire nand_1_out, nand_2_out, not_1_out;

  not not_1 (not_1_out, D);
  nand nand_1 (nand_1_out, D, CLK);
  nand nand_2 (nand_2_out, not_1_out, CLK);
  nand nand_3 (Q, nand_1_out, Q_prime);
  nand nand_4 (Q_prime, Q, nand_2_out);
endmodule

module FrequencyCounter (
  input  [1:0] Sel,
  output out_2,
  output f,
  output f_2,
  output f_4,
  output f_8
);

  wire clk_out, d_ff_1_qn, d_ff_2_qn, d_ff_3_qn;

  Clock clk (.out(clk_out));
  not not_1 (f, clk_out);
  D_Flip_Flop d_ff_1 (.clk(clk_out), .D(d_ff_1_qn), .Q(f_2), .Qn(d_ff_1_qn));  // open: preset, en, reset
  D_Flip_Flop d_ff_2 (.clk(d_ff_1_qn), .D(d_ff_2_qn), .Q(f_4), .Qn(d_ff_2_qn));  // open: preset, en, reset
  D_Flip_Flop d_ff_3 (.clk(d_ff_2_qn), .D(d_ff_3_qn), .Q(f_8), .Qn(d_ff_3_qn));  // open: preset, en, reset
  Multiplexer #(.select(2), .enable("false")) multiplexer_1 (
    .in0(f_8), .in1(f_4), .in2(f_2), .in3(f), .out(out_2), .sel(Sel));
endmodule
