// Logisim project PhaseLockLoop.circ as structural Verilog: 2 circuits, main circuit PhaseLockLoop
// PLL
module PhaseLockLoop (
  output PLL
);

  wire Clock_out, d_flipflop_2_q, d_flipflop_q_prime;

  Clock Clock (.out(Clock_out));
  Dflipflop d_flipflop (.D(d_flipflop_2_q), .CLK(Clock_out), .Q_prime(d_flipflop_q_prime));  // open: Q
  Dflipflop d_flipflop_2 (.D(d_flipflop_q_prime), .CLK(Clock_out), .Q(d_flipflop_2_q), .Q_prime(PLL));
endmodule

module Dflipflop (
  input  D,
  input  CLK,
  output Q,
  output Q_prime
);

  wire nand_1_out, nand_2_out, not_1_out;

  not not_1 (not_1_out, D);
  nand nand_1 (nand_1_out, D, CLK);
  nand nand_2 (nand_2_out, not_1_out, CLK);
  nand nand_3 (Q, nand_1_out, Q_prime);
  nand nand_4 (Q_prime, Q, nand_2_out);
endmodule
