// Logisim project RomRam.circ as structural Verilog: 2 circuits, main circuit main
module main (
  input  in_1,
  input  in_2,
  input  [4:0] in_3,
  input  in_4,
  input  [5:0] Address,
  input  in_6,
  input  in_7,
  input  in_8,
  output out_9,
  output [3:0] out_10,
  output [5:0] out_11
);

  wire Clock_out;

  Clock Clock (.out(Clock_out));
  ROM #(.addrWidth(5), .dataWidth(4)) rom_1 (.addr(in_3), .data(out_10), .sel(in_4));
  RAM #(.addrWidth(6), .dataWidth(6)) ram_1 (
    .addr(Address), .data(out_11), .sel(in_6), .clk(Clock_out), .ld(in_7), .clr(in_8));
  _7_Segment_Display u_7_segment_display_1 (
    .g(out_11[1]), .f(out_11[0]), .a(in_7), .b(in_6), .e(out_11[2]), .d(out_11[3]), .c(out_11[4]),
    .dp(out_11[5]));
  assign out_9 = in_2 ? ~in_1 : 1'bz;  // Controlled_Inverter controlled_inverter_1

  // Notes on the sheet:
  //   contents of rom_1 (hex, n*v repeats v):
  //   3 1 1 4 0 1 1 0 1 1 1 0 0 1 0 0 0 4 0 1 0 1 0 0 0 1 0 1 1
endmodule

module Rom_referenc (
  input  [5:0] in_1,
  input  in_2,
  input  in_3,
  input  in_4,
  output [5:0] out_5
);

  wire Clock_out;

  Clock Clock (.out(Clock_out));
  RAM #(.addrWidth(6), .dataWidth(6)) ram_1 (
    .addr(in_1), .data(out_5), .sel(in_2), .clk(Clock_out), .ld(in_3), .clr(in_4));
endmodule
